// Logisim project COMPUTER1.circ as structural Verilog: 1 circuit, main circuit main
module main (
  input  TR,
  input  E_IN,
  input  [15:0] in_3,
  input  E_CLR,
  input  [7:0] in_5,
  output [11:0] out_6,
  output [15:0] out_7,
  output [11:0] PC,
  output [15:0] out_9,
  output [15:0] out_10,
  output S_OUT,
  output E_OUT,
  output [7:0] OUTR
);

  wire and_1_out, and_2_out, and_3_out, and_4_out, and_5_out, and_6_out, j_k_ff_1_q, main_1_p3, main_2_p4,
       main_6_p3, main_11_p6, not_1_out, not_2_out, not_3_out, not_4_out, not_5_out, or_1_out, P_out, r_out;
  wire [7:0] decoder_1_out0, main_10_p3;
  wire [11:0] bit_extender_1_out, main_9_p24;
  wire [15:0] main_1_p2, main_1_p4, ram_1_data;

  and and_1 (and_1_out, main_1_p4[11], P_out);
  // IR_main main_1: pin names not known; wires that end beside it: out_10[1], main_1_p2, main_1_p3, main_1_p4
  and and_2 (and_2_out, out_10[4], main_2_p4, decoder_1_out0[7]);
  Bit_Extender #(.in_width(16), .out_width(12)) bit_extender_1 (.in(main_1_p2), .out(bit_extender_1_out));
  not not_1 (not_1_out, decoder_1_out0[7]);
  // I_FF__main main_2: pin names not known; wires that end beside it: main_1_p4[15], main_1_p3, out_10[2], main_2_p4
  not not_2 (not_2_out, main_2_p4);
  and and_3 (and_3_out, not_2_out, out_10[4], decoder_1_out0[7]);
  not not_3 (not_3_out, main_2_p4);
  and r (r_out, not_3_out, decoder_1_out0[7], out_10[3]);
  and P (P_out, main_2_p4, decoder_1_out0[7], out_10[3]);
  // S_FF__main main_3: pin names not known; wires that end beside it: r_out, main_1_p4[0], main_1_p3, S_OUT
  not not_4 (not_4_out, 1'b1);
  Decoder #(.select(3), .enable("false")) decoder_1 (
    .out0(decoder_1_out0[0]), .out1(decoder_1_out0[1]), .out2(decoder_1_out0[2]), .out3(decoder_1_out0[3]),
    .out4(decoder_1_out0[4]), .out5(decoder_1_out0[5]), .out6(decoder_1_out0[6]), .out7(decoder_1_out0[7]),
    .sel(main_1_p4[14:12]));
  // SC_main main_4: pin names not known; wires that end beside it: decoder_1_out0[0], out_10[6], decoder_1_out0[1], decoder_1_out0[2], decoder_1_out0[3], out_10[5], decoder_1_out0[4], decoder_1_out0[5], decoder_1_out0[6], out_10[7], and_3_out, and_2_out, out_10, main_1_p3
  J_K_Flip_Flop j_k_ff_1 (
    .J(1'b1), .clk(main_1_p3), .K(not_4_out), .Q(j_k_ff_1_q), .reset(and_1_out));  // open: Qn, preset, en
  // AR_main main_5: pin names not known; wires that end beside it: bit_extender_1_out, not_1_out, main_2_p4, out_10[3], out_10[2], out_10[0], decoder_1_out0[5], out_10[4], out_6, main_1_p3
  // INPR_main main_6: pin names not known; wires that end beside it: in_5, main_1_p3, main_6_p3, main_1_p4[10], E_CLR
  and and_4 (and_4_out, decoder_1_out0[3], out_10[4]);
  and and_5 (and_5_out, decoder_1_out0[5], out_10[4]);
  or or_1 (or_1_out, and_4_out, and_5_out, and_6_out);
  and and_6 (and_6_out, decoder_1_out0[6], out_10[6]);
  // adder_AC_bus_main main_7: pin names not known; wires that end beside it: out_9, decoder_1_out0[0], out_10[5], decoder_1_out0[1], decoder_1_out0[2], P_out, main_1_p4[11], r_out, main_1_p4[9], main_1_p4[7], main_1_p4[6], main_1_p4[5], main_1_p4[11], r_out, main_1_p4[8], r_out, out_7, main_6_p3, main_1_p3, E_IN, E_OUT
  not not_5 (not_5_out, or_1_out);
  Clock clock_1 (.out(main_1_p3));
  RAM #(.addrWidth(12), .dataWidth(16)) ram_1 (
    .addr(out_6), .data(ram_1_data), .sel(1'b1), .clk(main_1_p3), .ld(not_5_out));  // open: clr
  assign ram_1_data = or_1_out ? main_1_p2 : 16'bz;  // Controlled_Buffer controlled_buffer_1
  // DR_main main_8: pin names not known; wires that end beside it: out_10[4], decoder_1_out0[0], decoder_1_out0[1], decoder_1_out0[2], decoder_1_out0[6], out_10[5], main_1_p2, out_7, main_1_p3
  // PC_main main_9: pin names not known; wires that end beside it: decoder_1_out0[4], out_10[4], decoder_1_out0[5], out_10[5], out_10[1], out_7, decoder_1_out0[6], out_10[6], r_out, out_9[15], main_1_p4[4], main_1_p4[3], main_1_p4[2], E_OUT, main_1_p4[1], P_out, j_k_ff_1_q, main_1_p4[9], 1'b1, main_1_p4[8], out_9, PC, main_1_p3, main_9_p24
  // OUTR_main main_10: pin names not known; wires that end beside it: P_out, main_1_p4[10], main_10_p3, main_1_p3, OUTR
  // BUS_main main_11: pin names not known; wires that end beside it: out_6, PC, out_7, out_9, main_1_p4, main_11_p6, ram_1_data, decoder_1_out0[0], decoder_1_out0[1], decoder_1_out0[2], decoder_1_out0[3], decoder_1_out0[4], decoder_1_out0[5], decoder_1_out0[6], decoder_1_out0[7], out_10[0], out_10[1], out_10[2], out_10[3], out_10[4], out_10[5], out_10[6], out_10[7], main_2_p4, P_out, main_1_p4[10], main_1_p2
  // TR_main main_12: pin names not known; wires that end beside it: TR, in_3, main_11_p6, main_1_p3
  Bit_Extender #(.in_width(16), .out_width(12)) bit_extender_2 (.in(main_1_p2), .out(main_9_p24));
  Bit_Extender #(.in_width(16), .out_width(8)) bit_extender_3 (.in(main_1_p2), .out(main_10_p3));

  // Notes on the sheet:
  //   IR
  //   I
  //   AR
  //   SC
  //   INPR
  //   AC-OUT
  //   AC
  //   AC
  //   DR
  //   BUS
endmodule
